# Fritzing sketch openLedRace_4_players (saved by Fritzing 0.9.3b)
breadboards: 1

parts:
  Componente1 = Arduino Uno (Rev3) - ICSP
  S1 = Momentary Switch [package=ksa_sealed_tac_switch]
  S2 = Momentary Switch [package=ksa_sealed_tac_switch]
  S3 = Momentary Switch [package=ksa_sealed_tac_switch]
  S4 = Momentary Switch [package=ksa_sealed_tac_switch]
  WS2813 = Neopixel Strip -- White (60/m)
  SP1 = SPEAKER [package=pcb_mount_speaker]
  C3 = Capacitor [package=cap-pth-small2]

nets:
  N1: Componente1.A0, S1.1
  N2: Componente1.A1, S2.1
  N3: Componente1.A2, S3.1
  N4: Componente1.A3, S4.1
  N5: Componente1.D2, WS2813.+5V
  N6: Componente1.D3_PWM, C3.1
  N7: Componente1.5V, WS2813.DI
  GND: Componente1.GND, S1.4, S2.4, S3.4, S4.4, WS2813.GND, SP1.+
  N8: SP1.-, C3.2

notes:
  For WS2813 led strip connect first LED to GND
  PIN 3 - Audio
  PIN 2 - LED strip
  PIN A0 - PLAYER 1 - RED
  PIN A1 - PLAYER 2 - BLUE
  PIN A2 - PLAYER 3 - GREEN
  PIN A3 - PLAYER 4 - YELLOW

custom parts:
  Neopixel Strip -- White (60/m): Neopixel Strip, White, 60 pixels per meter.
